# Fritzing sketch sensornode (saved by Fritzing 0.7.11b)
perfboards: 1

parts:
  MSP430G2432 = IC, DIP package, 20 pins [chip_label=MSP430G2432]
  R1 = Resistor [tolerance=±5% resistance=220 package=THT]
  nRF24L01+1 = shrouded pin header, 8 pins [form="♂ (shrouded male)"]
  -_pin = female pin header, 1 pin [form="♀ (female)"]
  +pin = female pin header, 1 pin [form="♀ (female)"]
  J1 = female pin header, 12 pins [form="♀ (female)"]
  J2 = female pin header, 12 pins [form="♀ (female)"]
  J3 = female pin header, 12 pins [form="♀ (female)"]
  Prototype_Area = female pin header, 11 pins [form="♀ (female)"]

nets:
  N1: MSP430G2432.pin1, R1.Pin_0, nRF24L01+1.pin8, +pin.pin1, J2.pin1
  N2: MSP430G2432.pin2, nRF24L01+1.pin5
  N3: MSP430G2432.pin3, nRF24L01+1.pin4
  N4: MSP430G2432.pin4, nRF24L01+1.pin6
  N5: MSP430G2432.pin5, nRF24L01+1.pin3
  N6: MSP430G2432.pin6, nRF24L01+1.pin7
  N7: MSP430G2432.pin7, nRF24L01+1.pin2
  N8: MSP430G2432.pin8, Prototype_Area.pin9
  N9: MSP430G2432.pin9, Prototype_Area.pin10
  N10: MSP430G2432.pin10, Prototype_Area.pin11
  N11: MSP430G2432.pin11, Prototype_Area.pin8
  N12: MSP430G2432.pin12, Prototype_Area.pin7
  N13: MSP430G2432.pin13, Prototype_Area.pin6
  N14: MSP430G2432.pin14, Prototype_Area.pin5
  N15: MSP430G2432.pin15, Prototype_Area.pin4
  N16: MSP430G2432.pin16, R1.Pin_1
  N17: MSP430G2432.pin17, Prototype_Area.pin3
  N18: MSP430G2432.pin18, Prototype_Area.pin2
  N19: MSP430G2432.pin19, Prototype_Area.pin1
  N20: MSP430G2432.pin20, nRF24L01+1.pin1, -_pin.pin1, J1.pin1
  N21: J1.pin2, J2.pin2, J3.pin2
  N22: J1.pin3, J2.pin3, J3.pin3
  N23: J1.pin4, J2.pin4, J3.pin4
  N24: J1.pin5, J2.pin5, J3.pin5
  N25: J1.pin6, J2.pin6, J3.pin6
  N26: J1.pin7, J2.pin7, J3.pin7
  N27: J1.pin8, J2.pin8, J3.pin8
  N28: J1.pin9, J2.pin9, J3.pin9
  N29: J1.pin10, J2.pin10, J3.pin10
  N30: J1.pin11, J2.pin11, J3.pin11
  N31: J1.pin12, J2.pin12, J3.pin12
